// Logisim project miops.circ as structural Verilog: 4 circuits, main circuit Processador
module Processador (
  input  in_1,
  output [1:0] SELETOR
);

  wire and_1_out, CLK, not_1_out, not_2_out, uc_1_aluop, uc_1_branch, uc_1_jump, uc_1_memread, uc_1_memwrite,
       uc_1_regdest, uc_1_regwrite, ula_1_out_5;
  wire [15:0] adder_1_out, bit_extender_1_out, bit_extender_4_out, register_1_q;
  wire [31:0] adder_2_out, banco_de_registradores_1_rg1_d, banco_de_registradores_1_rg2_d,
       bit_extender_3_out, Imediato, multiplexer_1_out, multiplexer_2_out, multiplexer_3_out,
       multiplexer_4_out, multiplexer_5_out, ram_1_data, rom_1_data, ula_1_out_4;

  Register #(.width(16)) register_1 (.D(bit_extender_1_out), .Q(register_1_q), .clk(CLK), .clr(in_1));  // open: en
  Bit_Extender #(.in_width(32)) bit_extender_1 (.in(multiplexer_4_out), .out(bit_extender_1_out));
  Clock clock_1 (.out(CLK));
  ROM #(.addrWidth(16), .dataWidth(32)) rom_1 (.addr(register_1_q), .data(rom_1_data));  // open: sel
  UC uc_1 (
    .a(rom_1_data[31]), .b(rom_1_data[30]), .c(rom_1_data[29]), .d(rom_1_data[28]), .regdest(uc_1_regdest),
    .jump(uc_1_jump), .branch(uc_1_branch), .memread(uc_1_memread), .aluop(uc_1_aluop),
    .memwrite(uc_1_memwrite), .regwrite(uc_1_regwrite), .out_12(SELETOR));
  Multiplexer #(.width(32), .enable("false")) multiplexer_1 (
    .in0(multiplexer_5_out), .in1(Imediato), .out(multiplexer_1_out), .sel(uc_1_regdest));
  assign Imediato = {{16{rom_1_data[15]}}, rom_1_data[15:0]};  // Bit_Extender bit_extender_2
  Adder #(.width(16)) adder_1 (.a(16'h1), .b(register_1_q), .out(adder_1_out));  // open: cin, cout
  not not_1 (not_1_out, CLK);
  assign bit_extender_3_out = {{16{adder_1_out[15]}}, adder_1_out};  // Bit_Extender bit_extender_3
  Banco_de_Registradores banco_de_registradores_1 (
    .rg_read1(rom_1_data[27:24]), .rg_read2(rom_1_data[19:16]), .write_data(multiplexer_1_out),
    .write_register(rom_1_data[23:20]), .clock(not_1_out), .clear(in_1), .uc(uc_1_regwrite),
    .rg1_d(banco_de_registradores_1_rg1_d), .rg2_d(banco_de_registradores_1_rg2_d));
  Multiplexer #(.width(32), .enable("false")) multiplexer_2 (
    .in0(banco_de_registradores_1_rg2_d), .in1(Imediato), .out(multiplexer_2_out), .sel(uc_1_aluop));
  Adder #(.width(32)) adder_2 (.a(bit_extender_3_out), .b(Imediato), .out(adder_2_out));  // open: cin, cout
  and and_1 (and_1_out, uc_1_branch, ula_1_out_5);
  Multiplexer #(.width(32), .enable("false")) multiplexer_3 (
    .in0(bit_extender_3_out), .in1(adder_2_out), .out(multiplexer_3_out), .sel(and_1_out));
  ULA ula_1 (
    .rg1_d(banco_de_registradores_1_rg1_d), .rg2_d(multiplexer_2_out), .UC(SELETOR), .out_4(ula_1_out_4),
    .out_5(ula_1_out_5));
  Multiplexer #(.width(32), .enable("false")) multiplexer_4 (
    .in0(multiplexer_3_out), .in1(adder_2_out), .out(multiplexer_4_out), .sel(uc_1_jump));
  Bit_Extender #(.in_width(32)) bit_extender_4 (.in(ula_1_out_4), .out(bit_extender_4_out));
  not not_2 (not_2_out, CLK);
  Multiplexer #(.width(32), .enable("false")) multiplexer_5 (
    .in0(ula_1_out_4), .in1(ram_1_data), .out(multiplexer_5_out), .sel(uc_1_memread));
  RAM #(.addrWidth(16), .dataWidth(32), .bus("separate")) ram_1 (
    .addr(bit_extender_4_out), .din(banco_de_registradores_1_rg2_d), .data(ram_1_data), .str(uc_1_memwrite),
    .clk(not_2_out), .ld(uc_1_memread));  // open: sel, clr

  // Other names for the same wires on the sheet: CLEAR = in_1

  // Notes on the sheet:
  //   contents of rom_1 (hex, n*v repeats v):
  //   0 40900000 40a00010 40b00020 40100000 40700004 6107001a 40200000 62070015 40000000 40300000 6307000c
  //   51470000 4430000 4490000 53570000 5520000 55a0000 24c00000 25d00000 5ced0000 e0000 13300001 8000fff3
  //   51670000 6620000 66b0000 36000000 12200001 8000ffea 11100001 8000ffe6
  //   MICRO-PROCESSADOR MIOPS
endmodule

// BANCO DE REGISTRADORES
module Banco_de_Registradores (
  input  [3:0] rg_read1,
  input  [3:0] rg_read2,
  input  [31:0] write_data,
  input  [3:0] write_register,
  input  clock,
  input  clear,
  input  uc,
  output [31:0] rg1_d,
  output [31:0] rg2_d
);

  wire en1, en2, en3, en4, en5, en6, en7, en8, en9, en10, en11, en12, en13, en14, en15, en16;
  wire [31:0] demultiplexer_2_out0, demultiplexer_2_out1, demultiplexer_2_out2, demultiplexer_2_out3,
       demultiplexer_2_out4, demultiplexer_2_out5, demultiplexer_2_out6, demultiplexer_2_out7,
       demultiplexer_2_out8, demultiplexer_2_out9, demultiplexer_2_out10, demultiplexer_2_out11,
       demultiplexer_2_out12, demultiplexer_2_out13, demultiplexer_2_out14, demultiplexer_2_out15, rg1, rg2,
       rg3, rg4, rg5, rg6, rg7, rg8, rg9, rg10, rg11, rg12, rg13, rg14, rg15, rg16;

  Demultiplexer #(.select(4)) demultiplexer_1 (
    .out0(en1), .out1(en2), .out2(en3), .out3(en4), .out4(en5), .out5(en6), .out6(en7), .out7(en8),
    .out8(en9), .out9(en10), .out10(en11), .out11(en12), .out12(en13), .out13(en14), .out14(en15),
    .out15(en16), .in(uc), .sel(write_register));  // open: en
  Demultiplexer #(.select(4), .width(32)) demultiplexer_2 (
    .out0(demultiplexer_2_out0), .out1(demultiplexer_2_out1), .out2(demultiplexer_2_out2),
    .out3(demultiplexer_2_out3), .out4(demultiplexer_2_out4), .out5(demultiplexer_2_out5),
    .out6(demultiplexer_2_out6), .out7(demultiplexer_2_out7), .out8(demultiplexer_2_out8),
    .out9(demultiplexer_2_out9), .out10(demultiplexer_2_out10), .out11(demultiplexer_2_out11),
    .out12(demultiplexer_2_out12), .out13(demultiplexer_2_out13), .out14(demultiplexer_2_out14),
    .out15(demultiplexer_2_out15), .in(write_data), .sel(write_register));  // open: en
  Register #(.width(32)) u_rg1 (.D(demultiplexer_2_out0), .en(en1), .Q(rg1), .clk(clock), .clr(clear));
  Register #(.width(32)) register_1 (.D(demultiplexer_2_out1), .en(en2), .Q(rg2), .clk(clock), .clr(clear));
  Register #(.width(32)) register_2 (.D(demultiplexer_2_out2), .en(en3), .Q(rg3), .clk(clock), .clr(clear));
  Register #(.width(32)) register_3 (.D(demultiplexer_2_out3), .en(en4), .Q(rg4), .clk(clock), .clr(clear));
  Register #(.width(32)) register_4 (.D(demultiplexer_2_out4), .en(en5), .Q(rg5), .clk(clock), .clr(clear));
  Register #(.width(32)) register_5 (.D(demultiplexer_2_out5), .en(en6), .Q(rg6), .clk(clock), .clr(clear));
  Register #(.width(32)) register_6 (.D(demultiplexer_2_out6), .en(en7), .Q(rg7), .clk(clock), .clr(clear));
  Register #(.width(32)) register_7 (.D(demultiplexer_2_out7), .en(en8), .Q(rg8), .clk(clock), .clr(clear));
  Register #(.width(32)) register_8 (.D(demultiplexer_2_out8), .en(en9), .Q(rg9), .clk(clock), .clr(clear));
  Register #(.width(32)) register_9 (.D(demultiplexer_2_out9), .en(en10), .Q(rg10), .clk(clock), .clr(clear));
  Register #(.width(32)) register_10 (.D(demultiplexer_2_out10), .en(en11), .Q(rg11), .clk(clock), .clr(clear));
  Register #(.width(32)) register_11 (.D(demultiplexer_2_out11), .en(en12), .Q(rg12), .clk(clock), .clr(clear));
  Register #(.width(32)) register_12 (.D(demultiplexer_2_out12), .en(en13), .Q(rg13), .clk(clock), .clr(clear));
  Register #(.width(32)) register_13 (.D(demultiplexer_2_out13), .en(en14), .Q(rg14), .clk(clock), .clr(clear));
  Register #(.width(32)) register_14 (.D(demultiplexer_2_out14), .en(en15), .Q(rg15), .clk(clock), .clr(clear));
  Register #(.width(32)) register_15 (.D(demultiplexer_2_out15), .en(en16), .Q(rg16), .clk(clock), .clr(clear));
  Multiplexer #(.select(4), .width(32)) multiplexer_1 (
    .in0(rg1), .in1(rg2), .in2(rg3), .in3(rg4), .in4(rg5), .in5(rg6), .in6(rg7), .in7(rg8), .in8(rg9),
    .in9(rg10), .in10(rg11), .in11(rg12), .in12(rg13), .in13(rg14), .in14(rg15), .in15(rg16), .out(rg1_d),
    .sel(rg_read1));  // open: en
  Multiplexer #(.select(4), .width(32)) multiplexer_2 (
    .in0(rg1), .in1(rg2), .in2(rg3), .in3(rg4), .in4(rg5), .in5(rg6), .in6(rg7), .in7(rg8), .in8(rg9),
    .in9(rg10), .in10(rg11), .in11(rg12), .in12(rg13), .in13(rg14), .in14(rg15), .in15(rg16), .out(rg2_d),
    .sel(rg_read2));  // open: en

  // Other names for the same wires on the sheet: clk = clock; clr = clear
endmodule

module ULA (
  input  [31:0] rg1_d,
  input  [1:0] UC,
  input  [31:0] rg2_d,
  output [31:0] out_4,
  output out_5
);

  wire [31:0] adder_1_out, bit_extender_1_out, multiplier_1_out, subtractor_1_out;

  Adder #(.width(32)) adder_1 (.a(rg1_d), .b(rg2_d), .out(adder_1_out));  // open: cin, cout
  Subtractor #(.width(32)) subtractor_1 (.a(rg1_d), .b(rg2_d), .out(subtractor_1_out));  // open: bin, bout
  Comparator #(.width(32)) comparator_1 (.a(rg1_d), .b(rg2_d), .eq(out_5));  // open: gt, lt
  Multiplier #(.width(32)) multiplier_1 (.a(rg2_d), .b(rg1_d), .out(multiplier_1_out));  // open: cin, cout
  assign bit_extender_1_out = {{31{1'b0}}, out_5};  // Bit_Extender bit_extender_1
  Multiplexer #(.select(2), .width(32)) multiplexer_1 (
    .in0(adder_1_out), .in1(subtractor_1_out), .in2(multiplier_1_out), .in3(bit_extender_1_out), .out(out_4),
    .sel(UC));  // open: en
endmodule

module UC (
  input  a,
  input  b,
  input  c,
  input  d,
  output regdest,
  output jump,
  output branch,
  output memread,
  output aluop,
  output memwrite,
  output regwrite,
  output [1:0] out_12
);

  wire and_1_out, and_2_out, and_5_out, and_6_out, and_7_out, and_9_out, and_10_out, and_11_out, and_12_out,
       and_13_out, not_1_out, not_2_out, not_3_out, not_4_out, not_5_out, not_6_out, not_7_out, not_8_out,
       not_9_out, not_10_out, not_11_out, not_12_out, not_13_out, not_14_out, not_15_out, not_16_out,
       not_17_out;

  not not_1 (not_1_out, c);
  and and_1 (and_1_out, b, not_1_out, not_2_out);
  not not_2 (not_2_out, d);
  and and_2 (and_2_out, a, d);
  and and_3 (branch, b, c, not_3_out);
  not not_3 (not_3_out, d);
  not not_4 (not_4_out, b);
  and and_4 (memread, not_4_out, c, not_5_out);
  not not_5 (not_5_out, d);
  not not_6 (not_6_out, b);
  and and_5 (and_5_out, not_6_out, d);
  not not_7 (not_7_out, b);
  and and_6 (and_6_out, not_7_out, c);
  not not_8 (not_8_out, c);
  and and_7 (and_7_out, b, not_8_out, not_9_out);
  not not_9 (not_9_out, d);
  not not_10 (not_10_out, b);
  and and_8 (memwrite, not_10_out, c, d);
  not not_11 (not_11_out, a);
  not not_12 (not_12_out, b);
  and and_9 (and_9_out, not_11_out, not_12_out, not_13_out);
  not not_13 (not_13_out, d);
  not not_14 (not_14_out, a);
  and and_10 (and_10_out, not_14_out, not_15_out);
  not not_15 (not_15_out, c);
  and and_11 (and_11_out, b, d);
  not not_16 (not_16_out, c);
  and and_12 (and_12_out, b, not_16_out, d);
  and and_13 (and_13_out, b, c, not_17_out);
  not not_17 (not_17_out, d);
  and and_14 (out_12[0], b, c);
  or or_1 (regdest, and_1_out, and_2_out);
  or or_2 (aluop, and_5_out, and_6_out, and_7_out, a);
  or or_3 (regwrite, and_9_out, and_10_out, and_11_out);
  or or_4 (out_12[1], and_12_out, and_13_out);

  assign jump = a;
endmodule
